# Fritzing sketch Examen_de_Medio_Curso (saved by Fritzing 0.9.5d)
breadboards: 2

parts:
  LED1 = 7-SEGMENT-4DIGIT-YOUNGSUN [package=7-segment-4digit-youngsun-longpads]
  LED2 = 7-SEGMENT-4DIGIT-YOUNGSUN [package=7-segment-4digit-youngsun]
  R1 = Resistor [tolerance=±5% resistance=1k package="2512 [SMD]"]
  R2 = Resistor [tolerance=±5% resistance=1k package="2512 [SMD]"]
  R3 = Resistor [tolerance=±5% resistance=1k package="2512 [SMD]"]
  R4 = Resistor [tolerance=±5% resistance=1k package="2512 [SMD]"]
  R5 = Resistor [tolerance=±5% resistance=1k package="2512 [SMD]"]
  R6 = Resistor [tolerance=±5% resistance=1k package="2512 [SMD]"]
  R7 = Resistor [tolerance=±5% resistance=1k package="2512 [SMD]"]
  U1 = STM32F40x [package="LQFP64, 10x10mm"]
  IC1 = IC, DIP package, 16 pins [chip_label=74LS47]
  U2 = M74HC238 [package=dil16]
  S1 = Pushbutton [package="[SMD]"]
  U3 = POT [package=pot_mammoth]

nets:
  N1: LED1.DIG1, U2.Y0
  N2: LED1.DIG2, U2.Y1
  N3: LED1.D, LED2.D, R5.Pin_0
  N4: LED1.E, LED2.E, R4.Pin_0
  N5: LED1.DIG3, U2.Y2
  N6: LED1.DIG4, U2.Y3
  N7: LED1.F, LED2.F, R1.Pin_0
  N8: LED1.C, LED2.C, R6.Pin_0
  N9: LED1.A, LED2.A, R3.Pin_0
  N10: LED1.G, LED2.G, R2.Pin_0
  N11: LED1.B, LED2.B, R7.Pin_0
  N12: LED2.DIG1, U2.Y4
  N13: LED2.DIG2, U2.Y5
  N14: LED2.DIG3, U2.Y6
  N15: LED2.DIG4, U2.Y7
  N16: R1.Pin_1, IC1.pin15
  N17: R2.Pin_1, IC1.pin14
  N18: R3.Pin_1, IC1.pin13
  N19: R4.Pin_1, IC1.pin9
  N20: R5.Pin_1, IC1.pin10
  N21: R6.Pin_1, IC1.pin11
  N22: R7.Pin_1, IC1.pin12
  N23: U1.V5, IC1.pin3, IC1.pin4, IC1.pin5, IC1.pin16, U2.G1, U2.VCC, U3.E
  N24: U1.PC0, IC1.pin7
  N25: U1.PC1, IC1.pin1
  N26: U1.PD0, IC1.pin2
  N27: U1.PD1, IC1.pin6
  N28: U1.PD2, U2.A
  N29: U1.PD3, U2.B
  N30: U1.PD4, U2.C
  N31: U1.PB0, U3.A
  N32: U1.PB1, S1.Pin_1, S1.Pin_2
  N33: U1.VDD4, IC1.pin8, U2.~G2A, U2.~G2B, U2.GND, S1.Pin_3, S1.Pin_4, U3.S

custom parts:
  STM32F40x: STM32F405xx and STM32F407xx microcontroller in LQFP64 pinout. ARM Cortex-M4 32b MCU+FPU
