# Fritzing sketch Control ON-OFF (saved by Fritzing 0.9.5d)
breadboards: 1

parts:
  R2 = Resistor [tolerance=±5% resistance=100 package=THT]
  U1 = STM32F40x [package="LQFP64, 10x10mm"]
  T1 = LM35 Temperature Sensor [package="TO92 [THT]"]
  VCC1 = Battery block 9V
  LED1 = RGB LED (com. cathode, rgb) [package="5 mm [THT]"]
  R3 = Resistor [tolerance=±5% resistance=220 package=THT]
  R4 = Resistor [tolerance=±5% resistance=220 package=THT]
  R5 = Resistor [tolerance=±5% resistance=220 package=THT]
  R6 = Resistor [tolerance=±5% resistance=100 package=THT]
  L298N1 = L298N DC motor driver

nets:
  N1: R2.Pin_0, R6.Pin_0, L298N1.OUT3
  N2: R2.Pin_1, R6.Pin_1, L298N1.OUT4
  N3: U1.V5, T1.+Vs
  N4: U1.PC1, T1.Vout
  N5: U1.PD12, R4.Pin_0
  N6: U1.PA5, L298N1.IN4
  N7: U1.PD14, R3.Pin_0
  N8: U1.PD15, R5.Pin_0
  GND: U1.VDD4, T1.GND, VCC1.-, LED1.common_cathode, L298N1.GND
  N9: VCC1.+, L298N1.12V
  N10: LED1.red_anode, R3.Pin_1
  N11: LED1.green_anode, R4.Pin_1
  N12: LED1.blue_anode, R5.Pin_1
  N13: L298N1.5V#9, L298N1.ENA
  N14: L298N1.5V#10, L298N1.ENB

notes:
  El esquematico del paquete del diver L298N no funciona correctamente.
  Por eso no es mostrado.

custom parts:
  STM32F40x: STM32F405xx and STM32F407xx microcontroller in LQFP64 pinout. ARM Cortex-M4 32b MCU+FPU
  L298N DC motor driver: 2x DC motor driver with 78M05 positive voltage regulator (7..35 V) L298N: max 46 V, 2 A Set 5 V Enable jumper to enable 5 V regultor (needed for the L298N) and +5 V output at screw terminal or supply external +5 V at screw terminal Set ENA and/or ENB to +5 V to enable motor permanently or supply ENA and/or ENB with PWM signal IN1 and IN2 set rotation directory for motor A (OUT1/OUT2) IN2 and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
